// Digital circuit CPU.dig as structural Verilog
module CPU (
  input  [7:0] Input,
  input  _2Hz,
  input  _100Hz,
  output [7:0] Output
);

  wire and_1_out, and_2_out, and_3_out, and_4_out, and_5_out, and_6_out, and_8_out, and_9_out, and_10_out,
       and_11_out, and_12_out, and_13_out, and_14_out, and_23_out, and_24_out, and_25_out, and_27_out,
       and_28_out, and_29_out, and_30_out, and_31_out, and_32_out, and_33_out, and_34_out, and_36_out,
       and_37_out, and_38_out, and_39_out, and_41_out, and_42_out, and_43_out, buttonled_1_p1,
       buttonled_1_p2, buttonled_2_p1, buttonled_2_p2, buttonled_3_p1, buttonled_3_p2, Clk, Counter_Cnt,
       Data_Str, DepthsMatch, dipswitch_1_out, Dir, Enable, EndOfAddr, nand_1_out, nand_2_out, nClk,
       nCntr_Clr, nInput_Await, NonZero, nor_1_out, nor_2_out, nor_3_out, nor_4_out, nor_5_out, nor_6_out,
       not_1_out, not_3_out, not_4_out, not_5_out, not_6_out, nPntr_Clr, nReset_out, nRst, nSeek,
       nSeekTrigger, nStep_Rst, or_1_out, or_2_out, or_6_out, or_7_out, or_8_out, or_9_out, or_10_out,
       or_11_out, or_12_out, Pulse_out, rs_ff_as_1_q, rs_ff_as_2_q, rs_ff_as_3_nq, rs_ff_as_3_q,
       rs_ff_as_4_q, rs_ff_as_8_nq, rs_ff_as_9_q, rs_ff_as_10_q, rs_ff_as_11_nq, rs_ff_as_12_q,
       rs_ff_as_13_q, rs_ff_as_14_q, Rst, Seek, SeekTrigger, Send_out, xor_3_out;
  wire [2:0] Step;
  wire [3:3] counter4_1_out;
  wire [7:0] Changer_p6, counter16_1_out, counter16_1_out_2, Data, not_2_out, register8_1_q, register8_2_q,
       register8_3_q, rom_1_d, uCode_A_d, uCode_B_d;
  wire [12:0] and_26_out;
  wire [15:0] Addr, ProgAddr;

  or or_1 (or_1_out, dipswitch_1_out, EndOfAddr);
  DipSwitch dipswitch_1 (.out(dipswitch_1_out));
  and and_1 (and_1_out, Clk, or_1_out);
  DipSwitch #(.dipDefault("true")) nReset (.out(nReset_out));
  RS_FF_AS rs_ff_as_1 (.S(and_1_out), .R(and_6_out), .Q(rs_ff_as_1_q));  // open: nQ
  RS_FF_AS rs_ff_as_2 (.S(and_6_out), .R(Rst), .Q(rs_ff_as_2_q));  // open: nQ
  not not_1 (not_1_out, nReset_out);
  and and_2 (and_2_out, nReset_out, nClk);
  and and_3 (and_3_out, nClk, rs_ff_as_1_q);
  and and_4 (and_4_out, nClk, rs_ff_as_2_q);
  RS_FF_AS rs_ff_as_3 (.S(not_1_out), .R(and_2_out), .Q(rs_ff_as_3_q), .nQ(rs_ff_as_3_nq));
  and and_5 (and_5_out, rs_ff_as_3_nq, Clk);
  LED led_1 (.in(Clk));
  LED led_2 (.in(Rst));
  LED led_3 (.in(nCntr_Clr));
  LED led_4 (.in(nPntr_Clr));
  LED led_5 (.in(EndOfAddr));
  LED led_6 (.in(Data_Str));
  LED led_7 (.in(Data_Str));
  LED led_8 (.in(Enable));
  RS_FF_AS rs_ff_as_4 (.S(and_3_out), .R(and_6_out), .Q(rs_ff_as_4_q), .nQ(nCntr_Clr));
  RS_FF_AS rs_ff_as_5 (.S(and_4_out), .R(Rst), .Q(Enable));  // open: nQ
  and and_6 (and_6_out, Clk, rs_ff_as_4_q);
  and and_7 (nPntr_Clr, nCntr_Clr, nRst);
  RS_FF_AS rs_ff_as_6 (.S(Rst), .R(rs_ff_as_4_q), .Q(Data_Str));  // open: nQ
  RS_FF_AS rs_ff_as_7 (.S(rs_ff_as_3_q), .R(and_5_out), .Q(Rst), .nQ(nRst));
  or or_2 (or_2_out, and_6_out, buttonled_1_p1);
  // ButtonLED buttonled_1: pin names not known; wires that end beside it: buttonled_1_p1, buttonled_1_p2
  // ButtonLED buttonled_2: pin names not known; wires that end beside it: buttonled_2_p1, buttonled_2_p2
  // ButtonLED buttonled_3: pin names not known; wires that end beside it: buttonled_3_p1, buttonled_3_p2
  assign not_2_out = ~rom_1_d;  // Not not_2, 8 bits wide
  and and_8 (and_8_out, rom_1_d[0], rom_1_d[1], not_2_out[2], rom_1_d[3]);
  and and_9 (and_9_out, rom_1_d[0], not_2_out[1], rom_1_d[2], rom_1_d[3]);
  and and_10 (and_10_out, not_2_out[0], not_2_out[1], rom_1_d[2], rom_1_d[3]);
  and and_11 (and_11_out, not_2_out[0], rom_1_d[1], rom_1_d[2], rom_1_d[3]);
  and and_12 (and_12_out, not_2_out[4], rom_1_d[5], not_2_out[6], not_2_out[7]);
  and and_13 (and_13_out, rom_1_d[4], rom_1_d[5], not_2_out[6], not_2_out[7]);
  and and_14 (and_14_out, rom_1_d[4], not_2_out[5], rom_1_d[6], not_2_out[7]);
  nor nor_1 (nor_1_out, buttonled_2_p2, buttonled_3_p2);
  nor nor_2 (nor_2_out, buttonled_1_p2, buttonled_3_p2);
  nor nor_3 (nor_3_out, buttonled_1_p2, buttonled_2_p2);
  ROM #(.AddrBits(16), .Bits(8)) rom_1 (.A(ProgAddr), .sel(1'b1), .D(rom_1_d));
  // Probe on ProgAddr
  or or_3 (buttonled_1_p2, or_2_out, nor_1_out);
  or or_4 (buttonled_2_p2, buttonled_2_p1, nor_2_out);
  or or_5 (buttonled_3_p2, buttonled_3_p1, nor_3_out);
  and and_15 (and_26_out[5], and_8_out, and_12_out);
  and and_16 (and_26_out[6], and_9_out, and_12_out);
  and and_17 (and_26_out[7], and_10_out, and_12_out);
  and and_18 (and_26_out[8], and_11_out, and_12_out);
  and and_19 (and_26_out[9], and_10_out, and_13_out);
  and and_20 (and_26_out[10], and_13_out, and_11_out);
  and and_21 (and_26_out[11], and_14_out, and_8_out);
  and and_22 (and_26_out[12], and_9_out, and_14_out);
  and and_23 (and_23_out, buttonled_1_p2, Pulse_out);
  Button Pulse (.out(Pulse_out));
  and and_24 (and_24_out, buttonled_2_p2, _2Hz);
  and and_25 (and_25_out, buttonled_3_p2, _100Hz);
  LED plus (.in(and_26_out[5]));
  LED led_9 (.in(and_26_out[6]));
  LED led_10 (.in(and_26_out[7]));
  LED led_11 (.in(and_26_out[8]));
  LED lt (.in(and_26_out[9]));
  LED gt (.in(and_26_out[10]));
  LED led_12 (.in(and_26_out[11]));
  LED led_13 (.in(and_26_out[12]));
  or or_6 (or_6_out, and_24_out, and_25_out);
  or or_7 (or_7_out, and_23_out, or_6_out);
  nand nand_1 (nand_1_out, and_26_out[0], nInput_Await);
  LED led_14 (.in(or_7_out));
  xor xor_1 (Clk, or_7_out, 1'b0);
  xor xor_2 (nClk, or_7_out, 1'b1);
  Counter4 counter4_1 (
    .nPL(nStep_Rst), .nU_D(1'b0), .CP(nClk), .nCE(nand_1_out), .In(4'b0000), .Out({counter4_1_out[3], Step}));  // open: nRC
  and and_26 (and_26_out[0], rs_ff_as_8_nq, Enable);
  // Probe on Step
  ROM #(.AddrBits(13), .Bits(8)) uCode_A (.A({and_26_out[12:5], Step, Seek, and_26_out[0]}), .sel(1'b1), .D(uCode_A_d));
  ROM #(.AddrBits(13), .Bits(8)) uCode_B (.A({and_26_out[12:5], Step, Seek, and_26_out[0]}), .sel(1'b1), .D(uCode_B_d));
  RS_FF_AS rs_ff_as_8 (.S(Counter_Cnt), .R(nClk), .nQ(rs_ff_as_8_nq));  // open: Q
  LED Output_In (.in(uCode_B_d[4]));
  LED TrySeek (.in(uCode_B_d[3]));
  LED TryStopSeek (.in(uCode_B_d[2]));
  LED TryLatchDepth (.in(uCode_B_d[1]));
  LED CountDepth (.in(uCode_B_d[0]));
  LED Input_Await (.in(uCode_B_d[6]));
  LED Input_Out (.in(uCode_B_d[5]));
  LED Data_In (.in(uCode_A_d[0]));
  LED Data_Out (.in(uCode_B_d[7]));
  LED Pointer_Inc (.in(uCode_A_d[6]));
  LED Pointer_Dec (.in(uCode_A_d[5]));
  LED Changer_Add (.in(uCode_A_d[4]));
  LED Changer_Sub (.in(uCode_A_d[3]));
  LED Changer_In (.in(uCode_A_d[2]));
  LED Changer_Out (.in(uCode_A_d[1]));
  LED u_Counter_Cnt (.in(uCode_A_d[7]));
  not not_3 (not_3_out, uCode_B_d[6]);
  RS_FF_AS rs_ff_as_9 (.S(not_3_out), .R(Send_out), .Q(rs_ff_as_9_q));  // open: nQ
  Button Send (.out(Send_out));
  and and_27 (and_27_out, uCode_B_d[3], SeekTrigger);
  RS_FF_AS rs_ff_as_10 (.S(Send_out), .R(uCode_B_d[5]), .Q(rs_ff_as_10_q));  // open: nQ
  and and_28 (and_28_out, uCode_B_d[2], DepthsMatch);
  xor xor_3 (xor_3_out, and_26_out[12], Dir);
  and and_29 (and_29_out, Clk, uCode_A_d[7]);
  and and_30 (and_30_out, Clk, rs_ff_as_14_q);
  nor nor_4 (nor_4_out, uCode_A_d[3], uCode_A_d[4]);
  and and_31 (and_31_out, uCode_B_d[6], rs_ff_as_9_q);
  Register8 register8_1 (.nEn(1'b0), .D(Input), .Clk(Send_out), .Q(register8_1_q));
  or or_8 (or_8_out, Rst, and_28_out);
  and and_32 (and_32_out, and_27_out, and_26_out[12]);
  and and_33 (and_33_out, xor_3_out, nSeekTrigger);
  not not_4 (not_4_out, uCode_B_d[0]);
  RS_FF_AS rs_ff_as_11 (.S(and_29_out), .R(and_30_out), .Q(Counter_Cnt), .nQ(rs_ff_as_11_nq));
  and and_34 (and_34_out, rs_ff_as_10_q, nClk);
  and and_35 (nStep_Rst, nRst, rs_ff_as_11_nq);
  nor nor_5 (nor_5_out, Rst, uCode_A_d[2]);
  assign Data = uCode_A_d[1] ? Changer_p6 : 8'bz;  // Driver driver_1
  and and_36 (and_36_out, and_31_out, Clk);
  assign Data = uCode_B_d[5] ? register8_1_q : 8'bz;  // Driver driver_2
  RS_FF_AS rs_ff_as_12 (.S(and_34_out), .R(uCode_B_d[5]), .Q(rs_ff_as_12_q));  // open: nQ
  JK_FF jk_ff_1 (.J(and_27_out), .C(~nClk), .K(or_8_out), .Q(Seek), .nQ(nSeek));
  JK_FF jk_ff_2 (.J(and_32_out), .C(~nClk), .K(or_8_out), .Q(Dir));  // open: nQ
  and and_37 (and_37_out, nSeek, SeekTrigger);
  Counter16 counter16_1 (
    .nPL(nRst), .nU_D(and_33_out), .CP(Clk), .nCE(not_4_out), .In({16{1'b0}}),
    .Out({counter16_1_out_2, counter16_1_out}));  // open: nRC
  and and_38 (and_38_out, Counter_Cnt, nClk);
  // Counter8 Changer: pin names not known; wires that end beside it: nor_5_out, uCode_A_d[3], Clk, nor_4_out, Data, Changer_p6
  RS_FF_AS rs_ff_as_13 (.S(and_36_out), .R(or_9_out), .Q(rs_ff_as_13_q), .nQ(nInput_Await));
  or or_9 (or_9_out, Rst, and_39_out);
  LED u_Seek (.in(Seek));
  LED u_Dir (.in(Dir));
  nand nand_2 (nand_2_out, and_37_out, uCode_B_d[1]);
  Counter16 Counter (
    .nPL(nCntr_Clr), .nU_D(Dir), .CP(nClk), .nCE(rs_ff_as_11_nq), .In({16{1'b0}}), .Out(ProgAddr));  // open: nRC
  RS_FF_AS rs_ff_as_14 (.S(and_38_out), .R(and_30_out), .Q(rs_ff_as_14_q));  // open: nQ
  LED led_15 (.in(rs_ff_as_13_q));
  and and_39 (and_39_out, rs_ff_as_12_q, Clk);
  Register8 register8_2 (.nEn(nand_2_out), .D(counter16_1_out), .Clk(Clk), .Q(register8_2_q));
  Register8 register8_3 (.nEn(nand_2_out), .D(counter16_1_out_2), .Clk(Clk), .Q(register8_3_q));
  or or_10 (or_10_out, uCode_A_d[6], uCode_A_d[5]);
  not not_5 (not_5_out, uCode_B_d[4]);
  nor nor_6 (nor_6_out, Data_Str, or_10_out);
  or or_11 (or_11_out, uCode_A_d[0], Data_Str);
  not not_6 (not_6_out, NonZero);
  and and_40 (SeekTrigger, or_12_out, nSeek);
  Equal equal_1 (.A({register8_3_q, register8_2_q}), .B({counter16_1_out_2, counter16_1_out}), .Eq(DepthsMatch));
  Counter16 Pointer (
    .nPL(nPntr_Clr), .nU_D(uCode_A_d[5]), .CP(Clk), .nCE(nor_6_out), .In({16{1'b0}}), .Out(Addr));  // open: nRC
  RAMDualPort #(.AddrBits(16), .Bits(8)) u_Data (
    .A(Addr), .Din(Data), .str(or_11_out), .C(Clk), .ld(uCode_B_d[7]), .D(Data));
  PullDown #(.Bits(8)) pulldown_1 (.out(Data));
  and and_41 (and_41_out, uCode_B_d[4], Clk);
  Register8 register8_4 (.nEn(not_5_out), .D(Data), .Clk(Clk), .Q(Output));
  and and_42 (and_42_out, and_26_out[12], NonZero);
  and and_43 (and_43_out, not_6_out, and_26_out[11]);
  not not_7 (nSeekTrigger, SeekTrigger);
  // Probe on Addr
  // Probe on Data
  LED led_16 (.in(and_41_out));
  or or_12 (or_12_out, and_42_out, and_43_out);
  // Probe on {register8_3_q, register8_2_q}
  // Probe on {counter16_1_out_2, counter16_1_out}
  EndOfAddress endofaddress_1 (.D(Addr), .End(EndOfAddr));
  Nonzero nonzero_1 (.D(Data), .NZ(NonZero));
  LED Seek_Trigger (.in(SeekTrigger));

  // Other names for the same wires on the sheet: Pntr_Up = Data_Str

  // Notes on the sheet:
  //   _2Hz: Hz: 2
  //   _100Hz: Hz: 100
  //   RAM chip connections:
  //   ~WE = Data_In NAND +Clk
  //   ~OE = DATA_Out
  //   ~CS = 0
  //   Alternatively:
  //   LowerRAM.~CS = A_15
  //   UpperRAM.~CS = NOT A_15
  //   Initialization Sequencing
  //   Reset Timing
  //   EndOfAddress goes
  //   high on -Clk when
  //   the wiping process is complete
  //   EndOfAddress will be
  //   determined by the value
  //   of Cntr
  //   Wire colors:
  //   Clock lines - yellow
  //   Step lines/logic - red
  //   Decoding logic - green
  //   Decision logic - blue
  //   Manupulation logic - white
  //   Signal Display
  //   Decode
  //   Clock Generation
  //   rom_1 loads program.bf
  //   Control Microcode
  //   uCode_A loads ucodeA.bin
  //   uCode_B loads ucodeB.bin
  //   Input
  //   Seek/Dir Latching
  //   Depth Counting/Comparison
  //   Counter
  //   Data Changer
  //   Depth
  //   Pointer
  //   Data
  //   Output
  //   Seek Trigger
  //   Target Depth
  //   Current Depth
endmodule
